# Fritzing sketch circuit diagram (saved by Fritzing 0.8.7b)
breadboards: 1

parts:
  IC1 = MCP3008 8-channel 10-bit ADC [part_number=MCP3008]
  Raspberry_Pi_Zero1 = Raspberry Pi Zero
  T1 = MCP9700-E/TO Temperature Sensor [package="TO92 [THT]"]
  IC3 = 24LC01 [package="SO8 [SMD]"]
  S1 = Pushbutton [package="[THT]"]
  SG1 = Buzzer 12mm [package=buzzer-ccv]

nets:
  N1: IC1.no_name_yet#2, T1.Vout
  GND: IC1.no_name_yet#9, IC1.no_name_yet#14, Raspberry_Pi_Zero1.GND, T1.GND
  N2: IC1.no_name_yet#10, Raspberry_Pi_Zero1.GIPO8
  N3: IC1.no_name_yet#11, Raspberry_Pi_Zero1.GIPO10
  N4: IC1.no_name_yet#12, Raspberry_Pi_Zero1.GIPO9
  N5: IC1.no_name_yet#13, Raspberry_Pi_Zero1.GIPO11
  3V3: IC1.no_name_yet#15, IC1.no_name_yet#16, Raspberry_Pi_Zero1.3v3, Raspberry_Pi_Zero1.3V3, T1.+Vs
  N6: Raspberry_Pi_Zero1.GPIO2, IC3.SDA_-_I2C_Data
  N7: Raspberry_Pi_Zero1.GPIO3, IC3.SCL_-_I2C_Clock
  N8: Raspberry_Pi_Zero1.GIPO12, SG1.1
  N9: Raspberry_Pi_Zero1.GIPO23, S1.Pin_3, S1.Pin_4
  N10: Raspberry_Pi_Zero1.5V, IC3.+V
  GND_2: IC3.0V, S1.Pin_2, SG1.2

custom parts:
  MCP9700-E/TO Temperature Sensor: A MCP9700-E/TO temperature sensor with a temperature range from -40°C to 125°C.
